# Fritzing sketch AruinoStrain3 (saved by Fritzing 0.9.3b)
circuit board: 8.46667cm x 5.64444cm

parts:
  Microcontroller = Arduino Uno (Rev3)
  SD_Shield = Arduino MicroSD Shield
  AD623c = IC, DIP package, 8 pins [chip_label=IC]
  AD623b = IC, DIP package, 8 pins [chip_label=IC]
  AD623a = IC, DIP package, 8 pins [chip_label=IC]
  SG2 = Photocell (LDR) [package=THT]
  SG3 = Photocell (LDR) [package=THT]
  SG1 = Photocell (LDR) [package=THT]
  R1 = Resistor [tolerance=±0.1% resistance=120 package=THT]
  R2a = Resistor [tolerance=±0.1% resistance=120 package=THT]
  R2b = Resistor [tolerance=±0.1% resistance=120 package=THT]
  R2c = Resistor [tolerance=±0.1% resistance=120 package=THT]
  R4 = Resistor [tolerance=±0.1% resistance=120 package=THT]
  Rg = Resistor [tolerance=±1% resistance=100k package=THT]

nets:
  N1: Microcontroller.D8, SD_Shield.CS
  N2: Microcontroller.D11_PWM/MOSI, SD_Shield.MOSI
  N3: Microcontroller.D12/MISO, SD_Shield.MISO
  N4: Microcontroller.D13/SCK, SD_Shield.SCK
  N5: Microcontroller.GND, SD_Shield.N$91
  5V: Microcontroller.5V, SD_Shield.5V, SD_Shield.N$24, SD_Shield.N$31, SD_Shield.N$34, SD_Shield.N$47, SD_Shield.N$57, SD_Shield.N$58, SD_Shield.N$112, SD_Shield.N$119, SD_Shield.N$141, SD_Shield.N$148, AD623c.pin4, AD623c.pin7, AD623b.pin4, AD623b.pin7, AD623a.pin4, AD623a.pin7, R1.Pin_1, R2a.Pin_0, R2b.Pin_0, R2c.Pin_0
  N6: SD_Shield.GND, SD_Shield.N$50, SD_Shield.N$138, SD_Shield.N$145, SD_Shield.N$173, AD623c.pin5, AD623b.pin5, AD623a.pin5, SG2.pin_1, SG3.pin_1, SG1.pin_1, R4.Pin_1
  N7: SD_Shield.A0, SD_Shield.N$135, AD623a.pin6
  N8: SD_Shield.A1, SD_Shield.N$128, AD623b.pin6
  N9: SD_Shield.A2, SD_Shield.N$41, AD623c.pin6
  N10: SD_Shield.N$15, SD_Shield.N$65, SD_Shield.N$102, SD_Shield.N$109, AD623c.pin8, AD623b.pin8, AD623a.pin8, Rg.Pin_1
  N11: SD_Shield.N$18, SD_Shield.N$99, SD_Shield.N$106, SD_Shield.N$172, AD623c.pin1, AD623b.pin1, AD623a.pin1, Rg.Pin_0
  N12: SD_Shield.N$21, SD_Shield.N$115, SD_Shield.N$122, SD_Shield.N$177, SD_Shield.N$178, AD623c.pin2, AD623b.pin2, AD623a.pin2, R1.Pin_0, R4.Pin_0
  N13: SD_Shield.N$27, SD_Shield.N$44, AD623c.pin3, SG3.pin_0, R2c.Pin_1
  N14: SD_Shield.N$38, SD_Shield.N$125, AD623b.pin3, SG2.pin_0, R2b.Pin_1
  N15: SD_Shield.N$53, SD_Shield.N$132, AD623a.pin3, SG1.pin_0, R2a.Pin_1

// code stored in the sketch: FastStrainGauge.ino
//SD.h 
//#include <SPI.h>
//#include <SD.h>
//File dataFile;

//SdFat.h 
#include <SPI.h>
#include <SdFat.h>
SdFat sd;
SdFile dataFile;

const byte CS_PIN  = 4; // Chip Select Pin 8 for Sparkfun MicroSD shield
const byte analogPin0 = A0;   
const byte analogPin1 = A1;   
const byte analogPin2 = A2; 

int val = 0; 

void setup () {
  Serial.begin(115200);
//  Serial.println("Type any Character to begin");
//  while (Serial.read() <= 0) { }

  Serial.println("Initializing Card");
  pinMode(CS_PIN, OUTPUT);
 
  if (!sd.begin(CS_PIN))//SdFat.h syntax
//  if(!SD.begin(CS_PIN))//SD.h syntax
  {
    Serial.println("Card Failure");
    while(1);
  }
  Serial.println("Card Ready");

  if (dataFile.open("ANALOG_DATA.csv", O_RDWR | O_CREAT | O_AT_END)) //SdFat syntax
   
//    dataFile = SD.open("ConstantWriteTest.csv",FILE_WRITE);//SD.h
//    if(dataFile)//Sd.h
  {
    Serial.println("data file open");
    dataFile.print("Data Point Number, Analog Reading 1, Analog Reading 2, Analog Reading 3, Current Milliseconds, Microseconds Write Time");
  }
  else
  {
    Serial.println("error opening file");
    while(1);
  }
}

void loop () { 
 
  static unsigned long recordNumber=0;
  static unsigned long lastWrite = micros();
  dataFile.print(recordNumber++);
  dataFile.print(",");
  dataFile.print(analogRead(analogPin0));
  dataFile.print(",");
  dataFile.print(analogRead(analogPin1));
  dataFile.print(",");
  dataFile.print(analogRead(analogPin2));
  dataFile.print(",");
  dataFile.print(millis());
  dataFile.print(",");
  dataFile.println(micros() - lastWrite);
  lastWrite = micros();


      
  static unsigned long chunkTime = 5000;
  static unsigned long startLog = millis();
  // Save data after 20 seconds
  
  if ((millis() - startLog) > chunkTime) {
    dataFile.close();
    Serial.println("close file");
    if (dataFile.open("ANALOG_DATA.csv", O_RDWR | O_CREAT | O_AT_END)) //SdFat syntax
   
//    dataFile = SD.open("ConstantWriteTest.csv",FILE_WRITE);//SD.h
//    if(dataFile)//Sd.h
  {
    Serial.println("data file open");
    startLog += chunkTime;
  }
  else
  {
    Serial.println("error opening file");
    while(1);
  }
}
}
